// Logisim project AG_przejscia_idk.circ as structural Verilog: 1 circuit, main circuit main
module main (
);

  wire and_1_out, and_2_out, and_3_out, and_4_out, and_5_out, and_6_out, dipswitch_1_p1, dipswitch_1_p2,
       dipswitch_1_p3, not_1_out, not_2_out, not_3_out, not_4_out, not_5_out, not_6_out, or_1_out, or_2_out;

  // DipSwitch #(.number(3)) dipswitch_1: pin names not known; wires that end beside it: dipswitch_1_p1, dipswitch_1_p2, dipswitch_1_p3
  LED led_1 (.in(not_1_out));
  not not_1 (not_1_out, dipswitch_1_p1);
  or or_1 (or_1_out, and_1_out, and_2_out);
  LED led_2 (.in(or_1_out));
  and and_1 (and_1_out, not_2_out, dipswitch_1_p2);
  not not_2 (not_2_out, dipswitch_1_p1);
  and and_2 (and_2_out, dipswitch_1_p1, not_3_out);
  not not_3 (not_3_out, dipswitch_1_p2);
  not not_4 (not_4_out, dipswitch_1_p1);
  or or_2 (or_2_out, and_3_out, and_4_out, and_5_out);
  LED led_3 (.in(or_2_out));
  and and_3 (and_3_out, not_4_out, dipswitch_1_p3);
  and and_4 (and_4_out, not_5_out, dipswitch_1_p3);
  not not_5 (not_5_out, dipswitch_1_p2);
  and and_5 (and_5_out, dipswitch_1_p1, dipswitch_1_p2, not_6_out);
  not not_6 (not_6_out, dipswitch_1_p3);
  and and_6 (and_6_out, dipswitch_1_p1, dipswitch_1_p2, dipswitch_1_p3);
  LED led_4 (.in(and_6_out));

  // Notes on the sheet:
  //   a
  //   b
  //   c
endmodule
