// Logisim project Lab3z3.circ as structural Verilog: 1 circuit, main circuit main
module main (
);

  wire nand_1_out, nand_2_out, nand_3_out, not_1_out, slider_1_out;

  Slider #(.width(1)) slider_1 (.out(slider_1_out));
  not not_1 (not_1_out, slider_1_out);
  nand nand_1 (nand_1_out, 1'b1, slider_1_out);
  nand nand_2 (nand_2_out, 1'b1, not_1_out);
  nand nand_3 (nand_3_out, nand_1_out, nand_2_out);
  LED led_1 (.in(nand_3_out));

  // Notes on the sheet:
  //   A
  //   B
  //   S
  //   Y = ((A*S)'*(B*S')')'
  //   Y = A*!S +B*S
  //   Y = !(!(A*S)*!(B*!S)
endmodule
