// Logisim project Pnawias_z1z2_plus_z2z1_Rnawias_gwiazdka_z1z1.circ as structural Verilog: 1 circuit, main circuit main
module main (
);

  wire and_1_out, and_2_out, and_3_out, and_4_out, and_5_out, and_6_out, CLK_out, JK0_q, JK0_qn, JK1_q,
       JK1_qn, JK2_qn, not_1_out, not_2_out, or_1_out, or_2_out, or_3_out, RST_out, undriven, Z_out;

  Button Z (.out(Z_out));
  not not_1 (not_1_out, Z_out);
  Clock CLK (.out(CLK_out));
  and and_1 (and_1_out, JK1_qn, JK2_qn, not_1_out);
  J_K_Flip_Flop JK0 (
    .J(and_1_out), .K(or_1_out), .clk(CLK_out), .Q(JK0_q), .Qn(JK0_qn), .reset(RST_out));  // open: preset
  or or_1 (or_1_out, JK1_q, Z_out);
  and and_2 (and_2_out, JK2_qn, Z_out, JK0_qn);
  and and_3 (and_3_out, Z_out, JK0_q);
  J_K_Flip_Flop JK1 (.J(or_2_out), .K(1'b1), .clk(CLK_out), .Q(JK1_q), .Qn(JK1_qn), .reset(RST_out));  // open: preset
  or or_2 (or_2_out, and_2_out, and_3_out);
  Button RST (.out(RST_out));
  and and_4 (and_4_out, JK1_q, JK0_q);
  and and_5 (and_5_out, JK1_q, Z_out);
  J_K_Flip_Flop JK2 (.J(or_3_out), .K(undriven), .clk(CLK_out), .Qn(JK2_qn), .reset(RST_out));  // open: Q, preset
  or or_3 (or_3_out, and_4_out, and_5_out);
  // NoConnect on undriven
  and and_6 (and_6_out, JK1_qn, not_2_out, JK0_q);
  not not_2 (not_2_out, Z_out);
  LED Y (.in(and_6_out));
endmodule
