// Logisim project SRNOR_latch.circ as structural Verilog: 1 circuit, main circuit main
module main (
);

  wire button_1_out, button_2_out, nor_1_out, nor_2_out;

  Button button_1 (.out(button_1_out));
  Button button_2 (.out(button_2_out));
  nor nor_1 (nor_1_out, button_1_out, nor_2_out);
  nor nor_2 (nor_2_out, nor_1_out, button_2_out);
  LED led_1 (.in(nor_1_out));
  LED led_2 (.in(nor_2_out));
endmodule
