// Logisim project lab2.circ as structural Verilog
module main (
);

  wire dipswitch_1_p1, dipswitch_1_p2, dipswitch_1_p3, dipswitch_1_p4, nand_1_out, nand_2_out, nand_3_out,
       nand_4_out, nand_5_out;

  // DipSwitch #(.number(4)) dipswitch_1: pin names not known; wires that end beside it: dipswitch_1_p1, dipswitch_1_p2, dipswitch_1_p3, dipswitch_1_p4
  nand nand_1 (nand_1_out, dipswitch_1_p4, dipswitch_1_p2, dipswitch_1_p1);
  nand nand_2 (nand_2_out, dipswitch_1_p3, dipswitch_1_p2, dipswitch_1_p1);
  nand nand_3 (nand_3_out, dipswitch_1_p4, dipswitch_1_p3, dipswitch_1_p2);
  nand nand_4 (nand_4_out, dipswitch_1_p4, dipswitch_1_p3, dipswitch_1_p1);
  nand nand_5 (nand_5_out, nand_1_out, nand_2_out, nand_3_out, nand_4_out);
  LED led_1 (.in(nand_5_out));
endmodule

// VHDL entity Przycisk, as the project stores it:
--------------------------------------------------------------------------------
-- Project :
-- File    :
-- Autor   :
-- Date    :
--
--------------------------------------------------------------------------------
-- Description :
--
--------------------------------------------------------------------------------

LIBRARY ieee;
USE ieee.std_logic_1164.all;

ENTITY Przycisk IS
  PORT (
  ------------------------------------------------------------------------------
  --Insert input ports below
    clock      : IN  std_logic;                    -- input bit example
    val        : IN  std_logic_vector(3 DOWNTO 0); -- input vector example
  ------------------------------------------------------------------------------
  --Insert output ports below
    max        : OUT std_logic;                    -- output bit example
    cpt        : OUT std_logic_vector(3 DOWNTO 0)  -- output vector example
    );
END Przycisk;

--------------------------------------------------------------------------------
--Complete your VHDL description below
--------------------------------------------------------------------------------

ARCHITECTURE TypeArchitecture OF Przycisk IS

BEGIN


END TypeArchitecture;
