// Logisim project licznik_down_mod14_sync.circ as structural Verilog: 1 circuit, main circuit main
module main (
);

  wire and_1_out, and_2_out, and_3_out, and_4_out, button_1_out, clock_1_out, JK0_q, JK0_qn, JK1_q, JK1_qn,
       JK2_q, JK2_qn, JK3_q, or_1_out;

  J_K_Flip_Flop JK0 (
    .J(1'b1), .K(1'b1), .clk(clock_1_out), .Q(JK0_q), .Qn(JK0_qn), .reset(button_1_out));  // open: preset
  Clock clock_1 (.out(clock_1_out));
  Button button_1 (.out(button_1_out));
  LED led_1 (.in(JK0_q));
  LED led_2 (.in(JK1_q));
  and and_1 (and_1_out, JK3_q, JK0_qn);
  and and_2 (and_2_out, JK2_q, JK0_qn);
  LED led_3 (.in(JK2_q));
  or or_1 (or_1_out, JK1_q, and_1_out, and_2_out);
  J_K_Flip_Flop JK1 (
    .J(or_1_out), .K(JK0_qn), .clk(clock_1_out), .Q(JK1_q), .Qn(JK1_qn), .reset(button_1_out));  // open: preset
  LED led_4 (.in(JK3_q));
  J_K_Flip_Flop JK2 (
    .J(and_3_out), .K(and_3_out), .clk(clock_1_out), .Q(JK2_q), .Qn(JK2_qn), .reset(button_1_out));  // open: preset
  and and_3 (and_3_out, JK1_qn, JK0_qn);
  J_K_Flip_Flop JK3 (
    .J(and_4_out), .K(and_4_out), .clk(clock_1_out), .Q(JK3_q), .reset(button_1_out));  // open: Qn, preset
  and and_4 (and_4_out, JK2_qn, JK0_qn, JK1_qn);
endmodule
