// Logisim project licznik_mod_14_async.circ as structural Verilog: 1 circuit, main circuit main
module main (
);

  wire CLK_out, j_k_ff_1_q, j_k_ff_1_qn, j_k_ff_2_q, j_k_ff_2_qn, LSB_q, LSB_qn, MSB_q, nand_1_out, not_1_out;

  Clock CLK (.out(CLK_out));
  J_K_Flip_Flop LSB (.J(1'b1), .K(1'b1), .clk(CLK_out), .Q(LSB_q), .Qn(LSB_qn), .reset(not_1_out));  // open: preset
  LedBar ledbar_1 (
    .led0(LSB_q), .led1(LSB_q), .led2(j_k_ff_1_q), .led3(j_k_ff_1_q), .led4(j_k_ff_2_q), .led5(j_k_ff_2_q),
    .led6(MSB_q), .led7(MSB_q));
  J_K_Flip_Flop j_k_ff_1 (
    .J(1'b1), .K(1'b1), .clk(LSB_qn), .Q(j_k_ff_1_q), .Qn(j_k_ff_1_qn), .reset(not_1_out));  // open: preset
  J_K_Flip_Flop j_k_ff_2 (
    .J(1'b1), .K(1'b1), .clk(j_k_ff_1_qn), .Q(j_k_ff_2_q), .Qn(j_k_ff_2_qn), .reset(not_1_out));  // open: preset
  J_K_Flip_Flop MSB (.J(1'b1), .K(1'b1), .clk(j_k_ff_2_qn), .Q(MSB_q), .reset(not_1_out));  // open: Qn, preset
  nand nand_1 (nand_1_out, j_k_ff_1_q, j_k_ff_2_q, MSB_q);
  not not_1 (not_1_out, nand_1_out);

  // Notes on the sheet:
  //   2^0
  //   2^1
  //   2^2
  //   2^3
endmodule
