// Logisim project licznik_mod_14_sync.circ as structural Verilog: 1 circuit, main circuit main
module main (
);

  wire and_1_out, and_2_out, and_3_out, and_4_out, and_5_out, and_6_out, button_1_out, clock_1_out,
       dipswitch_1_p1, dipswitch_1_p2, dipswitch_1_p3, dipswitch_2_p1, dipswitch_2_p2, dipswitch_2_p3,
       dipswitch_3_p1, dipswitch_3_p2, dipswitch_3_p3, JK0_q, JK1_q, JK2_q, JK3_q, not_1_out, not_2_out,
       not_3_out, not_4_out, or_1_out, or_3_out;

  J_K_Flip_Flop JK0 (.J(1'b1), .K(1'b1), .clk(clock_1_out), .Q(JK0_q), .reset(button_1_out));  // open: Qn, preset
  Clock clock_1 (.out(clock_1_out));
  Button button_1 (.out(button_1_out));
  not not_1 (not_1_out, JK3_q);
  and and_1 (and_1_out, not_1_out, JK0_q);
  and and_2 (and_2_out, JK0_q, not_2_out);
  not not_2 (not_2_out, JK2_q);
  // DipSwitch #(.number(2)) dipswitch_1: pin names not known; wires that end beside it: dipswitch_1_p1, dipswitch_1_p2, dipswitch_1_p3
  // DipSwitch #(.number(2)) dipswitch_2: pin names not known; wires that end beside it: dipswitch_2_p1, dipswitch_2_p2, dipswitch_2_p3
  // DipSwitch #(.number(2)) dipswitch_3: pin names not known; wires that end beside it: dipswitch_3_p1, dipswitch_3_p2, dipswitch_3_p3
  J_K_Flip_Flop JK1 (.J(or_1_out), .K(JK0_q), .clk(clock_1_out), .Q(JK1_q), .reset(button_1_out));  // open: Qn, preset
  or or_1 (or_1_out, and_1_out, and_2_out);
  not not_3 (not_3_out, dipswitch_2_p1);
  not not_4 (not_4_out, dipswitch_2_p2);
  nor nor_1 (dipswitch_1_p3, dipswitch_1_p1, dipswitch_1_p2);
  or or_2 (dipswitch_2_p3, not_3_out, not_4_out);
  nand nand_1 (dipswitch_3_p3, dipswitch_3_p1, dipswitch_3_p2);
  LedBar #(.matrixcols(16)) ledbar_1 (
    .led0(JK0_q), .led1(JK0_q), .led2(JK0_q), .led3(JK0_q), .led4(JK1_q), .led5(JK1_q), .led6(JK1_q),
    .led7(JK1_q), .led8(JK2_q), .led9(JK2_q), .led10(JK2_q), .led11(JK2_q), .led12(JK3_q), .led13(JK3_q),
    .led14(JK3_q), .led15(JK3_q));
  and and_3 (and_3_out, JK0_q, JK1_q);
  and and_4 (and_4_out, JK0_q, or_3_out);
  or or_3 (or_3_out, JK1_q, JK3_q);
  J_K_Flip_Flop JK2 (
    .J(and_3_out), .K(and_4_out), .clk(clock_1_out), .Q(JK2_q), .reset(button_1_out));  // open: Qn, preset
  and and_5 (and_5_out, JK1_q, JK0_q, JK2_q);
  and and_6 (and_6_out, JK2_q, JK0_q);
  J_K_Flip_Flop JK3 (
    .J(and_5_out), .K(and_6_out), .clk(clock_1_out), .Q(JK3_q), .reset(button_1_out));  // open: Qn, preset
endmodule
