// Logisim project licznik_mod_4.circ as structural Verilog: 1 circuit, main circuit main
module main (
);

  wire and_1_out, CLK_out, JK0_q, JK0_qn, JK1_q, JK1_qn, JK2_q, JK2_qn, RST_out;

  and and_1 (and_1_out, JK1_q, JK0_q);
  Clock CLK (.out(CLK_out));
  Button RST (.out(RST_out));
  LED Q2 (.in(JK2_q));
  J_K_Flip_Flop JK2 (.J(and_1_out), .K(1'b1), .clk(CLK_out), .Q(JK2_q), .Qn(JK2_qn), .reset(RST_out));  // open: preset
  LED Q1 (.in(JK1_q));
  J_K_Flip_Flop JK1 (.J(JK0_q), .K(JK0_q), .clk(CLK_out), .Q(JK1_q), .Qn(JK1_qn), .reset(RST_out));  // open: preset
  // NoConnect on JK1_qn
  J_K_Flip_Flop JK0 (.J(JK2_qn), .K(1'b1), .clk(CLK_out), .Q(JK0_q), .Qn(JK0_qn), .reset(RST_out));  // open: preset
  LED Q0 (.in(JK0_q));
  // NoConnect on JK0_qn
endmodule
