// Logisim project mealy_1110_detektor_norm.circ as structural Verilog: 1 circuit, main circuit main
module main (
);

  wire and_1_out, and_2_out, CLK_out, j_k_ff_1_q, j_k_ff_2_q, j_k_ff_2_qn, not_1_out, or_1_out, Z_out;

  Button Z (.out(Z_out));
  Clock CLK (.out(CLK_out));
  not not_1 (not_1_out, Z_out);
  J_K_Flip_Flop j_k_ff_1 (.J(Z_out), .K(or_1_out), .clk(CLK_out), .Q(j_k_ff_1_q));  // open: Qn, preset, reset
  or or_1 (or_1_out, not_1_out, j_k_ff_2_qn);
  and and_1 (and_1_out, Z_out, j_k_ff_1_q);
  J_K_Flip_Flop j_k_ff_2 (
    .J(and_1_out), .K(not_1_out), .clk(CLK_out), .Q(j_k_ff_2_q), .Qn(j_k_ff_2_qn));  // open: preset, reset
  and and_2 (and_2_out, not_1_out, j_k_ff_1_q, j_k_ff_2_q);
  LED Y (.in(and_2_out));
endmodule
