// Logisim project mealy_detector_1110_nandy.circ as structural Verilog: 1 circuit, main circuit main
module main (
);

  wire CLK_out, d_ff_1_q, j_k_ff_1_q, j_k_ff_2_q, j_k_ff_2_qn, nand_1_out, nand_2_out, nor_1_out, not_1_out,
       not_2_out, not_3_out, not_4_out, Z_out;

  Button Z (.out(Z_out));
  Clock CLK (.out(CLK_out));
  not not_1 (not_1_out, Z_out);
  nor nor_1 (nor_1_out, not_1_out, j_k_ff_2_qn);
  not not_2 (not_2_out, nor_1_out);
  J_K_Flip_Flop j_k_ff_1 (.J(Z_out), .K(not_2_out), .clk(CLK_out), .Q(j_k_ff_1_q));  // open: Qn, preset, reset
  nand nand_1 (nand_1_out, Z_out, j_k_ff_1_q);
  J_K_Flip_Flop j_k_ff_2 (
    .J(not_3_out), .K(not_1_out), .clk(CLK_out), .Q(j_k_ff_2_q), .Qn(j_k_ff_2_qn));  // open: preset, reset
  not not_3 (not_3_out, nand_1_out);
  nand nand_2 (nand_2_out, not_1_out, j_k_ff_1_q, j_k_ff_2_q);
  not not_4 (not_4_out, nand_2_out);
  D_Flip_Flop d_ff_1 (.D(not_4_out), .clk(CLK_out), .Q(d_ff_1_q));  // open: Qn, preset, reset
  LED Y (.in(d_ff_1_q));
endmodule
