// Logisim project niedzialajacy_NFA.circ as structural Verilog: 1 circuit, main circuit main
module main (
  input  in_1
);

  wire and_1_out, and_2_out, and_3_out, and_4_out, and_5_out, and_6_out, nand_1_out, nor_1_out, nor_2_out,
       nor_3_out, nor_4_out, nor_5_out, nor_6_out, not_1_out, not_2_out, not_3_out, not_4_out, not_5_out,
       not_6_out, not_7_out, READ_out, RESET_out, RS1_q, RS2_q, RS2_qn, SET_out, Z0_out, Z1_out, Z2_out;

  Button READ (.out(READ_out));
  Button Z2 (.out(Z2_out));
  Button Z1 (.out(Z1_out));
  Button Z0 (.out(Z0_out));
  Button SET (.out(SET_out));
  Button RESET (.out(RESET_out));
  and and_1 (and_1_out, READ_out, in_1);
  and and_2 (and_2_out, in_1, Z2_out);
  nor nor_1 (nor_1_out, Z1_out, Z0_out);
  not not_1 (not_1_out, nor_1_out);
  nor nor_2 (nor_2_out, and_1_out, and_2_out);
  not not_2 (not_2_out, nor_2_out);
  and and_3 (and_3_out, RS1_q, not_1_out);
  and and_4 (and_4_out, RS2_qn, SET_out);
  nor nor_3 (nor_3_out, and_3_out, and_4_out);
  not not_3 (not_3_out, nor_3_out);
  S_R_Flip_Flop RS1 (.Q(RS1_q), .reset(not_4_out), .preset(not_3_out));  // open: S, R, clk, Qn
  LED C_RS1 (.in(RS1_q));
  nor nor_4 (nor_4_out, RS2_q, RESET_out);
  not not_4 (not_4_out, nor_4_out);
  and and_5 (and_5_out, not_2_out, RS1_q);
  and and_6 (and_6_out, Z2_out, RESET_out);
  nor nor_5 (nor_5_out, and_5_out, and_6_out);
  not not_5 (not_5_out, nor_5_out);
  nor nor_6 (nor_6_out, Z0_out, RESET_out);
  not not_6 (not_6_out, nor_6_out);
  S_R_Flip_Flop RS2 (.Q(RS2_q), .reset(not_6_out), .Qn(RS2_qn), .preset(not_5_out));  // open: S, R, clk
  LED C_RS2 (.in(RS2_q));
  nand nand_1 (nand_1_out, READ_out, RS2_q);
  not not_7 (not_7_out, nand_1_out);
  LED Y (.in(not_7_out));
endmodule
