// Logisim project proby_moore.circ as structural Verilog: 1 circuit, main circuit main
module main (
);

  wire and_1_out, CLK_out, JK0_q, JK1_q, JK1_qn, JK2_q, not_1_out, or_1_out, or_2_out, RST_out, Z_out;

  Button Z (.out(Z_out));
  Clock CLK (.out(CLK_out));
  J_K_Flip_Flop JK0 (.J(Z_out), .K(or_1_out), .clk(CLK_out), .Q(JK0_q), .reset(RST_out));  // open: Qn, preset
  or or_1 (or_1_out, JK2_q, JK1_qn);
  Button RST (.out(RST_out));
  and and_1 (and_1_out, Z_out, JK0_q);
  J_K_Flip_Flop JK1 (
    .J(or_2_out), .K(not_1_out), .clk(CLK_out), .Q(JK1_q), .Qn(JK1_qn), .reset(RST_out));  // open: preset
  or or_2 (or_2_out, and_1_out, JK1_q);
  not not_1 (not_1_out, Z_out);
  J_K_Flip_Flop JK2 (.J(JK2_q), .K(1'b1), .clk(CLK_out), .Q(JK2_q), .reset(RST_out));  // open: Qn, preset
  LED Y (.in(JK2_q));
endmodule
