// Logisim project regex_bez_nand.circ as structural Verilog: 1 circuit, main circuit main
module main (
  input  in_1
);

  wire and_1_out, and_2_out, and_3_out, and_4_out, button_1_out, clock_1_out, clock_2_out, clock_3_out,
       J0_gate_out, j_k_ff_1_q, j_k_ff_1_qn, j_k_ff_2_q, j_k_ff_2_qn, j_k_ff_3_qn, not_1_out, not_2_out,
       or_1_out, or_2_out, or_3_out;

  not not_1 (not_1_out, in_1);
  and J0_gate (J0_gate_out, not_1_out, j_k_ff_3_qn, j_k_ff_2_qn);
  not not_2 (not_2_out, j_k_ff_2_qn);
  and and_1 (and_1_out, j_k_ff_1_q, not_1_out);
  or or_1 (or_1_out, in_1, not_2_out);
  J_K_Flip_Flop j_k_ff_1 (
    .J(J0_gate_out), .K(or_1_out), .clk(clock_1_out), .Q(j_k_ff_1_q), .Qn(j_k_ff_1_qn), .reset(button_1_out));  // open: preset
  Clock clock_1 (.out(clock_1_out));
  and and_2 (and_2_out, in_1, j_k_ff_1_qn, j_k_ff_3_qn);
  J_K_Flip_Flop j_k_ff_2 (
    .J(or_2_out), .K(1'b1), .clk(clock_2_out), .Q(j_k_ff_2_q), .Qn(j_k_ff_2_qn), .reset(button_1_out));  // open: preset
  or or_2 (or_2_out, and_1_out, and_2_out);
  Clock clock_2 (.out(clock_2_out));
  LED led_1 (.in(and_3_out));
  and and_3 (and_3_out, j_k_ff_1_q, j_k_ff_2_q);
  and and_4 (and_4_out, in_1, j_k_ff_2_q);
  J_K_Flip_Flop j_k_ff_3 (
    .J(or_3_out), .K(1'b0), .clk(clock_3_out), .Qn(j_k_ff_3_qn), .reset(button_1_out));  // open: Q, preset
  or or_3 (or_3_out, and_3_out, and_4_out);
  Clock clock_3 (.out(clock_3_out));
  Button button_1 (.out(button_1_out));

  // Notes on the sheet:
  //   Z
  //   Q1
  //   Q0
  //   Z'
  //   Z'Q2'Q1'
  //   ZQ1
  //   Z
  //   Q0'
  //   Q2'
  //   Z'Q0
  //   ZQ0'Q2'
  //   Q0
  //   Q1
  //   Z
  //   Q1
endmodule
