// Logisim project regex_nand.circ as structural Verilog: 1 circuit, main circuit main
module main (
  input  Z
);

  wire clock_1_out, clock_2_out, clock_3_out, j_k_ff_1_q, j_k_ff_1_qn, j_k_ff_2_q, j_k_ff_2_qn, j_k_ff_3_qn,
       nand_1_out, nand_2_out, nand_3_out, nand_4_out, nand_5_out, nand_6_out, nand_7_out, nor_1_out,
       nor_2_out, nor_3_out, not_1_out, not_2_out, not_3_out, not_4_out, not_5_out, not_6_out, not_7_out,
       not_8_out, not_9_out, not_10_out, not_11_out, not_12_out, RST_out;

  not not_1 (not_1_out, Z);
  nand nand_1 (nand_1_out, not_1_out, j_k_ff_3_qn);
  not not_2 (not_2_out, nand_1_out);
  nand nand_2 (nand_2_out, not_2_out, j_k_ff_2_qn);
  not not_3 (not_3_out, nand_2_out);
  not not_4 (not_4_out, j_k_ff_2_qn);
  nor nor_1 (nor_1_out, Z, not_4_out);
  not not_5 (not_5_out, nor_1_out);
  nand nand_3 (nand_3_out, j_k_ff_1_q, not_1_out);
  not not_6 (not_6_out, nand_3_out);
  J_K_Flip_Flop j_k_ff_1 (
    .J(not_3_out), .K(not_5_out), .clk(clock_1_out), .Q(j_k_ff_1_q), .Qn(j_k_ff_1_qn), .reset(RST_out));  // open: preset
  Clock clock_1 (.out(clock_1_out));
  nand nand_4 (nand_4_out, Z, j_k_ff_1_qn);
  not not_7 (not_7_out, nand_4_out);
  nand nand_5 (nand_5_out, not_7_out, j_k_ff_3_qn);
  not not_8 (not_8_out, nand_5_out);
  J_K_Flip_Flop j_k_ff_2 (
    .J(not_9_out), .K(1'b1), .clk(clock_2_out), .Q(j_k_ff_2_q), .Qn(j_k_ff_2_qn), .reset(RST_out));  // open: preset
  nor nor_2 (nor_2_out, not_6_out, not_8_out);
  not not_9 (not_9_out, nor_2_out);
  Clock clock_2 (.out(clock_2_out));
  nand nand_6 (nand_6_out, j_k_ff_1_q, j_k_ff_2_q);
  nand nand_7 (nand_7_out, Z, j_k_ff_2_q);
  not not_10 (not_10_out, nand_7_out);
  not not_11 (not_11_out, nand_6_out);
  LED Y (.in(not_11_out));
  nor nor_3 (nor_3_out, not_11_out, not_10_out);
  not not_12 (not_12_out, nor_3_out);
  Clock clock_3 (.out(clock_3_out));
  J_K_Flip_Flop j_k_ff_3 (
    .J(not_12_out), .K(1'b0), .clk(clock_3_out), .Qn(j_k_ff_3_qn), .reset(RST_out));  // open: Q, preset
  Button RST (.out(RST_out));

  // Notes on the sheet:
  //   Z
  //   Q1
  //   Q0
  //   Z'
  //   Z'Q2'Q1'
  //   ZQ1
  //   Z
  //   Q0'
  //   Q2'
  //   Z'Q0
  //   ZQ0'Q2'
  //   Q0
  //   Q1
  //   Z
  //   Q1
endmodule
