// Logisim project schemat_detektora_1110_moore_na_dost_komponentach.circ as structural Verilog: 1 circuit, main circuit main
module main (
);

  wire CLK_out, JK0_q, JK1_q, JK1_qn, JK2_q, nand_1_out, nand_2_out, nand_3_out, nor_1_out, nor_2_out,
       not_1_out, not_2_out, not_3_out, not_4_out, not_5_out, not_6_out, not_7_out, RST_out, Z_out;

  Button Z (.out(Z_out));
  Clock CLK (.out(CLK_out));
  J_K_Flip_Flop JK0 (.J(Z_out), .K(not_1_out), .clk(CLK_out), .Q(JK0_q), .reset(RST_out));  // open: Qn, preset
  nor nor_1 (nor_1_out, not_7_out, JK1_qn);
  not not_1 (not_1_out, nor_1_out);
  Button RST (.out(RST_out));
  not not_2 (not_2_out, Z_out);
  nand nand_1 (nand_1_out, JK0_q, Z_out);
  not not_3 (not_3_out, nand_1_out);
  nor nor_2 (nor_2_out, not_3_out, JK1_q);
  J_K_Flip_Flop JK1 (
    .J(not_4_out), .K(not_5_out), .clk(CLK_out), .Q(JK1_q), .Qn(JK1_qn), .reset(RST_out));  // open: preset
  not not_4 (not_4_out, nor_2_out);
  not not_5 (not_5_out, Z_out);
  nand nand_2 (nand_2_out, JK0_q, JK1_q);
  not not_6 (not_6_out, nand_2_out);
  J_K_Flip_Flop JK2 (.J(not_7_out), .K(1'b1), .clk(CLK_out), .Q(JK2_q), .reset(RST_out));  // open: Qn, preset
  nand nand_3 (nand_3_out, not_2_out, not_6_out);
  not not_7 (not_7_out, nand_3_out);
  LED Y (.in(JK2_q));
endmodule
