// Logisim project srnorlatches.circ as structural Verilog: 1 circuit, main circuit main
module main (
);

  wire and_1_out, and_2_out, and_3_out, and_4_out, and_5_out, and_6_out, and_7_out, and_8_out, nor_1_out,
       nor_2_out, nor_3_out, nor_4_out, or_1_out, or_2_out, or_3_out, or_4_out, or_5_out, or_6_out, or_7_out,
       READ_out, RESET_out, START_out, Z0_out, Z1_out, Z2_out;

  Button READ (.out(READ_out));
  Button Z2 (.out(Z2_out));
  Button Z1 (.out(Z1_out));
  Button Z0 (.out(Z0_out));
  Button START (.out(START_out));
  Button RESET (.out(RESET_out));
  and and_1 (and_1_out, nor_3_out, Z1_out);
  or or_1 (or_1_out, Z1_out, Z0_out);
  and and_2 (and_2_out, READ_out, 1'b1);
  and and_3 (and_3_out, 1'b1, Z2_out);
  and and_4 (and_4_out, nor_1_out, or_1_out);
  or or_2 (or_2_out, and_2_out, and_3_out);
  or or_3 (or_3_out, and_4_out, and_5_out);
  and and_5 (and_5_out, START_out, nor_4_out);
  or or_4 (or_4_out, RESET_out, nor_3_out);
  LED SR1 (.in(nor_1_out));
  nor nor_1 (nor_1_out, or_4_out, nor_2_out);
  nor nor_2 (nor_2_out, nor_1_out, or_3_out);
  and and_6 (and_6_out, or_2_out, nor_1_out);
  and and_7 (and_7_out, Z2_out, nor_3_out);
  or or_5 (or_5_out, and_6_out, and_7_out);
  or or_6 (or_6_out, Z0_out, RESET_out);
  or or_7 (or_7_out, and_1_out, or_5_out);
  LED SR2 (.in(nor_3_out));
  nor nor_3 (nor_3_out, or_6_out, nor_4_out);
  nor nor_4 (nor_4_out, nor_3_out, or_7_out);
  and and_8 (and_8_out, READ_out, nor_3_out);
  LED Y (.in(and_8_out));
endmodule
